// Logisim project lab2.circ as structural Verilog: 4 circuits, main circuit 四位二进制可逆计数器
module \四位二进制可逆计数器  (
  input  in_1,
  input  in_2,
  input  in_3,
  output out_4,
  output out_5,
  output out_6,
  output out_7
);

  wire and_1_out, and_2_out, and_3_out, and_4_out, and_5_out, and_6_out, and_7_out, and_8_out, clock_1_out,
       not_1_out, not_2_out, not_3_out, nQA, nQB, nQC, nQD, or_1_out, or_2_out, or_3_out, or_4_out, or_5_out,
       xor_1_out, xor_2_out, xor_3_out, xor_4_out, xor_5_out, xor_6_out, xor_7_out;

  and and_1 (and_1_out, out_7, out_6, out_5);
  or or_1 (or_1_out, out_7, out_6, out_5);
  and and_2 (and_2_out, out_7, out_6);
  or or_2 (or_2_out, out_7, out_6);
  xor xor_1 (xor_1_out, out_4, and_1_out);
  not not_1 (not_1_out, out_4);
  xor xor_2 (xor_2_out, not_1_out, or_1_out);
  xor xor_3 (xor_3_out, out_5, and_2_out);
  not not_2 (not_2_out, out_5);
  xor xor_4 (xor_4_out, not_2_out, or_2_out);
  xor xor_5 (xor_5_out, out_7, out_6);
  not not_3 (not_3_out, out_7);
  xor xor_6 (xor_6_out, not_3_out, out_6);
  and and_3 (and_3_out, in_1, xor_1_out);
  and and_4 (and_4_out, in_3, xor_2_out);
  and and_5 (and_5_out, in_1, xor_3_out);
  and and_6 (and_6_out, in_3, xor_4_out);
  and and_7 (and_7_out, in_1, xor_5_out);
  and and_8 (and_8_out, in_3, xor_6_out);
  Clock clock_1 (.out(clock_1_out));
  or or_3 (or_3_out, and_3_out, and_4_out);
  or or_4 (or_4_out, and_5_out, and_6_out);
  or or_5 (or_5_out, and_7_out, and_8_out);
  D_Flip_Flop D (.clk(clock_1_out), .D(or_3_out), .Q(out_4), .Qn(nQD), .en(xor_7_out), .reset(in_2));  // open: preset
  D_Flip_Flop C (.clk(clock_1_out), .D(or_4_out), .Q(out_5), .Qn(nQC), .en(xor_7_out), .reset(in_2));  // open: preset
  D_Flip_Flop B (.clk(clock_1_out), .D(or_5_out), .Q(out_6), .Qn(nQB), .en(xor_7_out), .reset(in_2));  // open: preset
  D_Flip_Flop A (.clk(clock_1_out), .D(nQA), .Q(out_7), .Qn(nQA), .en(xor_7_out), .reset(in_2));  // open: preset
  xor xor_7 (xor_7_out, in_1, in_3);
  LED led_1 (.in(xor_7_out));

  // Other names for the same wires on the sheet: CLR = in_2; CPD = in_3; CPU = in_1; QA = out_7; QB = out_6;
  //   QC = out_5; QD = out_4

  // Notes on the sheet:
  //   绿灯表示正常运行
endmodule

module \一位16进制数转2位8421码  (
  input  in_1,
  input  in_2,
  input  in_3,
  input  in_4,
  output out_5,
  output out_6,
  output out_7,
  output out_8,
  output out_9,
  output out_10,
  output out_11,
  output out_12
);

  wire and_1_out, or_1_out;

  \四位二进制并行加法器  \u_四位二进制并行加法器_1  (
    .A3(in_1), .A2(in_2), .A1(in_3), .A0(in_4), .B3(1'b0), .B2(and_1_out), .B1(and_1_out), .B0(1'b0),
    .S3(out_9), .S2(out_10), .S1(out_11), .S0(out_12), .C0(1'b0), .C4(out_8));
  and and_1 (and_1_out, in_1, or_1_out);
  or or_1 (or_1_out, in_2, in_3);

  assign out_5 = 1'b0;
  assign out_6 = 1'b0;
  assign out_7 = 1'b0;

  // Other names for the same wires on the sheet: A0 = in_4; A1 = in_3; A2 = in_2; A3 = in_1; S0 = out_12; S1 = out_11;
  //   S2 = out_10; S3 = out_9; S4 = out_8
endmodule

module \_7段译码器  (
  input  in_1,
  input  in_2,
  input  in_3,
  input  in_4,
  output out_5,
  output out_6,
  output out_7,
  output out_8,
  output out_9,
  output out_10,
  output out_11
);

  wire and_1_out, and_2_out, and_3_out, and_4_out, and_5_out, and_6_out, and_7_out, and_8_out, and_9_out,
       and_10_out, and_11_out, and_12_out, and_13_out, and_14_out, and_15_out, and_16_out, and_17_out,
       and_18_out, not_1_out, not_2_out, not_3_out, not_4_out;

  not not_1 (not_1_out, in_2);
  not not_2 (not_2_out, in_1);
  not not_3 (not_3_out, in_4);
  not not_4 (not_4_out, in_3);
  and and_1 (and_1_out, not_2_out, not_1_out, not_4_out, in_4);
  and and_2 (and_2_out, not_2_out, in_2, not_4_out, not_3_out);
  and and_3 (and_3_out, not_2_out, in_2, not_4_out, in_4);
  and and_4 (and_4_out, not_2_out, in_2, in_3, not_3_out);
  and and_5 (and_5_out, not_2_out, not_1_out, not_4_out, in_4);
  and and_6 (and_6_out, not_2_out, in_2, not_4_out, not_3_out);
  and and_7 (and_7_out, not_2_out, in_2, in_3, in_4);
  and and_8 (and_8_out, not_2_out, not_1_out, not_4_out, not_3_out);
  and and_9 (and_9_out, not_2_out, not_1_out, in_3, not_3_out);
  and and_10 (and_10_out, not_2_out, in_2, in_3, not_3_out);
  and and_11 (and_11_out, in_1, not_1_out, not_4_out, not_3_out);
  and and_12 (and_12_out, not_2_out, not_1_out, not_4_out, in_4);
  and and_13 (and_13_out, not_2_out, not_1_out, in_3, not_3_out);
  and and_14 (and_14_out, not_2_out, not_1_out, in_3, in_4);
  and and_15 (and_15_out, not_2_out, in_2, in_3, in_4);
  and and_16 (and_16_out, not_2_out, not_1_out, not_4_out, not_3_out);
  and and_17 (and_17_out, not_2_out, not_1_out, not_4_out, in_4);
  and and_18 (and_18_out, not_2_out, in_2, in_3, in_4);
  nor nor_1 (out_5, and_1_out, and_2_out);
  nor nor_2 (out_6, and_3_out, and_4_out);
  nand nand_1 (out_7, not_2_out, not_1_out, in_3, not_3_out);
  nor nor_3 (out_8, and_5_out, and_6_out, and_7_out);
  or or_1 (out_9, and_8_out, and_9_out, and_10_out, and_11_out);
  nor nor_4 (out_11, and_16_out, and_17_out, and_18_out);
  nor nor_5 (out_10, and_12_out, and_13_out, and_14_out, and_15_out);

  // Other names for the same wires on the sheet: a = out_5; A0 = in_4; A1 = in_3; A2 = in_2; A3 = in_1; b = out_6;
  //   c = out_7; d = out_8; e = out_9; f = out_10; g = out_11
endmodule

module \_7段数码管显示  (
  input  [3:0] in_1
);

  wire \n7段译码器_1_out_5 , \n7段译码器_1_out_6 , \n7段译码器_1_out_7 , \n7段译码器_1_out_8 , \n7段译码器_1_out_9 ,
       \n7段译码器_1_out_10 , \n7段译码器_1_out_11 , \n7段译码器_2_out_5 , \n7段译码器_2_out_6 , \n7段译码器_2_out_7 ,
       \n7段译码器_2_out_8 , \n7段译码器_2_out_9 , \n7段译码器_2_out_10 , \n7段译码器_2_out_11 , \一位16进制数转2位8421码_1_out_5 ,
       \一位16进制数转2位8421码_1_out_6 , \一位16进制数转2位8421码_1_out_7 , \一位16进制数转2位8421码_1_out_8 ,
       \一位16进制数转2位8421码_1_out_9 , \一位16进制数转2位8421码_1_out_10 , \一位16进制数转2位8421码_1_out_11 ,
       \一位16进制数转2位8421码_1_out_12 ;

  // Probe on in_1
  \一位16进制数转2位8421码  \u_一位16进制数转2位8421码_1  (
    .in_1(in_1[3]), .in_2(in_1[2]), .in_3(in_1[1]), .in_4(in_1[0]), .out_5(\一位16进制数转2位8421码_1_out_5 ),
    .out_6(\一位16进制数转2位8421码_1_out_6 ), .out_7(\一位16进制数转2位8421码_1_out_7 ), .out_8(\一位16进制数转2位8421码_1_out_8 ),
    .out_9(\一位16进制数转2位8421码_1_out_9 ), .out_10(\一位16进制数转2位8421码_1_out_10 ),
    .out_11(\一位16进制数转2位8421码_1_out_11 ), .out_12(\一位16进制数转2位8421码_1_out_12 ));
  \_7段译码器  \u_7段译码器_1  (
    .in_1(\一位16进制数转2位8421码_1_out_5 ), .in_2(\一位16进制数转2位8421码_1_out_6 ), .in_3(\一位16进制数转2位8421码_1_out_7 ),
    .in_4(\一位16进制数转2位8421码_1_out_8 ), .out_5(\n7段译码器_1_out_5 ), .out_6(\n7段译码器_1_out_6 ),
    .out_7(\n7段译码器_1_out_7 ), .out_8(\n7段译码器_1_out_8 ), .out_9(\n7段译码器_1_out_9 ), .out_10(\n7段译码器_1_out_10 ),
    .out_11(\n7段译码器_1_out_11 ));
  \_7段译码器  \u_7段译码器_2  (
    .in_1(\一位16进制数转2位8421码_1_out_9 ), .in_2(\一位16进制数转2位8421码_1_out_10 ), .in_3(\一位16进制数转2位8421码_1_out_11 ),
    .in_4(\一位16进制数转2位8421码_1_out_12 ), .out_5(\n7段译码器_2_out_5 ), .out_6(\n7段译码器_2_out_6 ),
    .out_7(\n7段译码器_2_out_7 ), .out_8(\n7段译码器_2_out_8 ), .out_9(\n7段译码器_2_out_9 ), .out_10(\n7段译码器_2_out_10 ),
    .out_11(\n7段译码器_2_out_11 ));
  _7_Segment_Display u_7_segment_display_1 (
    .g(\n7段译码器_1_out_11 ), .f(\n7段译码器_1_out_10 ), .a(\n7段译码器_1_out_5 ), .b(\n7段译码器_1_out_6 ),
    .e(\n7段译码器_1_out_9 ), .d(\n7段译码器_1_out_8 ), .c(\n7段译码器_1_out_7 ));  // open: dp
  _7_Segment_Display u_7_segment_display_2 (
    .g(\n7段译码器_2_out_11 ), .f(\n7段译码器_2_out_10 ), .a(\n7段译码器_2_out_5 ), .b(\n7段译码器_2_out_6 ),
    .e(\n7段译码器_2_out_9 ), .d(\n7段译码器_2_out_8 ), .c(\n7段译码器_2_out_7 ));  // open: dp
  _7_Segment_Display u_7_segment_display_3 (
    .g(1'b1), .f(1'b1), .a(1'b1), .b(1'b0), .e(1'b1), .d(1'b1), .c(1'b1));  // open: dp

  // Notes on the sheet:
  //   人数
  //   转BCD
  //   7段译码器
  //   g
  //   f
  //   e
  //   d
  //   a
  //   b
  //   c
endmodule
